# Fritzing sketch Rangkaian NodeMCU Buzzer Aktif (saved by Fritzing 0.9.3b)

parts:
  Part1 = ESP Base Board For NodeMCU Amica Lolin dan ESP32
  NodeMCU_v1 = NodeMCU v3 LoLin [part_number=ESP8266]
  J1 = Piezo Speaker

nets:
  N1: Part1.6#215, Part1.2, NodeMCU_v1.D1
  N2: Part1.21#230, Part1.11, NodeMCU_v1.D8
  N3: Part1.1, Part1.6#245, Part1.15, Part1.26, NodeMCU_v1.D0, NodeMCU_v1.3V3
  N4: Part1.3, NodeMCU_v1.D2
  N5: Part1.4, NodeMCU_v1.D3
  N6: Part1.5, NodeMCU_v1.D4
  N7: Part1.7#246, Part1.14, Part1.25, Part1.29, Part1.21#290, NodeMCU_v1.GND#6, NodeMCU_v1.GND#13, NodeMCU_v1.GND#16, NodeMCU_v1.GND#33
  N8: Part1.8, NodeMCU_v1.D5
  N9: Part1.9#248, NodeMCU_v1.D6
  N10: Part1.10, NodeMCU_v1.D7
  N11: Part1.12, Part1.13, Part1.21#260, NodeMCU_v1.RX, NodeMCU_v1.TX, NodeMCU_v1.S1
  N12: Part1.16, NodeMCU_v1.A0
  N13: Part1.17, NodeMCU_v1.GND#41
  N14: Part1.18, NodeMCU_v1.VU
  N15: Part1.19, NodeMCU_v1.S3
  N16: Part1.20, NodeMCU_v1.S2
  N17: Part1.22, NodeMCU_v1.SC
  N18: Part1.23, NodeMCU_v1.S0
  N19: Part1.24, NodeMCU_v1.SK
  N20: Part1.27, NodeMCU_v1.EN
  N21: Part1.28, NodeMCU_v1.RST
  N22: Part1.30, NodeMCU_v1.VIN
  N23: Part1.7#276, J1.pin1
  N24: Part1.9#278, J1.pin2

notes:
  NodeMCU - Buzzer Module
  GND - GND
  I/O - D6
  VCC - 5V

custom parts:
  NodeMCU v3 LoLin: NodeMCU v3 LoLin NodeMCU (http://www.nodemcu.com/) is an open source IoT platform. It includes firmware (https://nodemcu-build.com/) which runs on the ESP8266 Wi-Fi SoC from Espressif Systems, and hardware which is based on the ESP-12E module. The term "NodeMCU" by default refers to the firmware rather than the dev kits. The firmware uses the Lua scripting language. It is based on the eLua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
